# Fritzing sketch nodemcu_rfid_buzzer (saved by Fritzing 0.9.3b)

parts:
  Part2 = RFID-RC522 [part_number=101218]
  J1 = Piezo Speaker  # not connected
  U1 = NodeMCU V1.0

nets:
  N1: Part2.SDA, U1.D4
  N2: Part2.SCK, U1.D5
  N3: Part2.MOSI, U1.D7
  N4: Part2.MISO, U1.D6
  GND: Part2.GND, U1.GND
  N5: Part2.RST, U1.D3
  3.3V: Part2.3.3V, U1.3V3

custom parts:
  NodeMCU V1.0: ESP8266 based NodeMCU
